// Logisim project rudimentary computing device.circ as structural Verilog: 1 circuit, main circuit main
module main (
  input  [5:0] in_1,
  input  [5:0] in_2,
  input  [5:0] in_3,
  input  in_4,
  output [5:0] out_5,
  output [5:0] out_6,
  output [5:0] out_7
);

  wire and_1_out, and_2_out, and_3_out, and_4_out, and_5_out, and_6_out, and_8_out, button_1_out,
       clock_1_out, main_2_a_b, main_2_a_b_2, main_2_a_b_3, main_2_add, main_2_halt, main_2_insert,
       main_2_invert, main_2_out, main_2_step;
  wire [0:0] main_4_equality_check, main_5_out_13, main_6_out_13;
  wire [5:0] and_13_out, main_1_out_14, main_3_out_4, main_7_out_12, main_9_out_19, main_10_to_a,
       main_10_to_b, main_10_to_c, main_11_p10, main_11_p21, main_12_p10, main_12_p21, main_13_p10,
       main_13_p21, main_14_out_8, main_14_out_9, main_14_out_10, main_15_out_8, main_15_out_9,
       main_15_out_10, main_16_out_8, main_16_out_9, main_16_out_10, main_17_out_8, main_17_out_9,
       main_17_out_10, main_18_out_8, main_18_out_9, main_18_out_10, main_19_out_8, main_19_out_9,
       main_19_out_10;
  wire [31:0] rom_1_data;

  Button button_1 (.out(button_1_out));
  and and_1 (and_1_out, in_4, main_2_halt);
  Clock clock_1 (.out(clock_1_out));
  program_counter_main main_1 (
    .in_7(button_1_out), .in_8(clock_1_out), .out_9(main_1_out_14[5]), .out_10(main_1_out_14[4]),
    .out_11(main_1_out_14[3]), .out_12(main_1_out_14[2]), .out_13(main_1_out_14[1]),
    .out_14(main_1_out_14[0]), .in_1(and_2_out), .in_2(and_3_out), .in_3(and_4_out), .in_4(and_5_out),
    .in_5(and_6_out), .in_6(and_8_out));
  and and_2 (and_2_out, in_4, and_13_out[5]);
  and and_3 (and_3_out, in_4, and_13_out[4]);
  instructor_main main_2 (
    .in_1(rom_1_data[30]), .in_2(rom_1_data[29]), .in_3(rom_1_data[28]), .in_4(rom_1_data[27]),
    .ADD(main_2_add), .INVERT(main_2_invert), .A_B(main_2_a_b), .A_B_2(main_2_a_b_2), .A_B_3(main_2_a_b_3),
    .STEP(main_2_step), .INSERT(main_2_insert), .OUT(main_2_out), .HALT(main_2_halt));  // open: out_14, out_15, out_16
  and and_4 (and_4_out, in_4, and_13_out[3]);
  step_selector_main main_3 (.in_2(main_13_p10[0]), .in_1(main_11_p10), .in_3(main_12_p10), .out_4(main_3_out_4));
  equality_check_main main_4 (
    .Equality_Check(main_4_equality_check[0]), .in_1(main_11_p10[5]), .in_2(main_11_p10[4]),
    .Number_A(main_11_p10[3]), .in_4(main_11_p10[2]), .in_5(main_11_p10[1]), .in_6(main_11_p10[0]),
    .in_7(main_12_p10[5]), .in_8(main_12_p10[4]), .in_9(main_12_p10[3]), .in_10(main_12_p10[2]),
    .in_11(main_12_p10[1]), .in_12(main_12_p10[0]));
  a_less_than_b_main main_5 (
    .in_7(main_12_p10[5]), .in_8(main_12_p10[4]), .in_9(main_12_p10[3]), .in_10(main_12_p10[2]),
    .in_11(main_12_p10[1]), .in_12(main_12_p10[0]), .in_1(main_11_p10[5]), .in_2(main_11_p10[4]),
    .in_3(main_11_p10[3]), .in_4(main_11_p10[2]), .in_5(main_11_p10[1]), .in_6(main_11_p10[0]),
    .out_13(main_5_out_13[0]));
  a_greater_than_b_main main_6 (
    .in_1(main_11_p10[5]), .in_2(main_11_p10[4]), .in_3(main_11_p10[3]), .in_4(main_11_p10[2]),
    .in_5(main_11_p10[1]), .in_6(main_11_p10[0]), .in_7(main_12_p10[5]), .in_8(main_12_p10[4]),
    .in_9(main_12_p10[3]), .in_10(main_12_p10[2]), .in_11(main_12_p10[1]), .in_12(main_12_p10[0]),
    .out_13(main_6_out_13[0]));
  inverter_main main_7 (
    .in_1(main_11_p10[5]), .in_2(main_11_p10[4]), .in_3(main_11_p10[3]), .in_4(main_11_p10[2]),
    .in_5(main_11_p10[1]), .in_6(main_11_p10[0]), .out_7(main_7_out_12[5]), .out_8(main_7_out_12[4]),
    .out_9(main_7_out_12[3]), .out_10(main_7_out_12[2]), .out_11(main_7_out_12[1]), .out_12(main_7_out_12[0]));
  input_selector_main main_8 (
    .in_4(main_2_out), .in_1({6{1'b0}}), .in_2({6{1'b0}}), .in_3({6{1'b0}}), .in_5(main_11_p10),
    .in_6(main_12_p10), .in_7(main_13_p10), .out_8(out_5), .out_9(out_6), .out_10(out_7));
  and and_5 (and_5_out, in_4, and_13_out[2]);
  addition_main main_9 (
    .in_1(main_12_p10[5]), .in_2(main_12_p10[4]), .in_3(main_12_p10[3]), .in_4(main_12_p10[2]),
    .in_5(main_12_p10[1]), .in_6(main_12_p10[0]), .in_7(main_11_p10[5]), .in_8(main_11_p10[4]),
    .in_9(main_11_p10[3]), .in_10(main_11_p10[2]), .in_11(main_11_p10[1]), .in_12(main_11_p10[0]),
    .out_14(main_9_out_19[5]), .out_15(main_9_out_19[4]), .out_16(main_9_out_19[3]),
    .out_17(main_9_out_19[2]), .out_18(main_9_out_19[1]), .out_19(main_9_out_19[0]));  // open: out_13
  ROM #(.addrWidth(6), .dataWidth(32)) rom_1 (.addr(main_1_out_14), .data(rom_1_data));  // open: sel
  and and_6 (and_6_out, in_4, and_13_out[1]);
  value_transfer_main main_10 (
    .Inp_A(main_11_p10), .Inp_C(main_13_p10), .Inp_B(main_12_p10), .To_B(main_10_to_b), .To_A(main_10_to_a),
    .To_C(main_10_to_c));
  and and_7 (and_13_out[5], main_3_out_4[5], main_2_step);
  // memory_small_main main_11: pin names not known; wires that end beside it: main_11_p10[5], rom_1_data[26], main_11_p10[4], rom_1_data[25], main_11_p10[3], rom_1_data[24], main_11_p10[2], main_11_p10[1], rom_1_data[23], main_11_p10[0], rom_1_data[22], rom_1_data[21], main_11_p21[5], rom_1_data[20], main_11_p21[4], rom_1_data[19], main_11_p21[3], main_11_p21[2], rom_1_data[18], main_11_p21[1], main_11_p21[0], button_1_out
  and and_8 (and_8_out, in_4, and_13_out[0]);
  and and_9 (and_13_out[4], main_3_out_4[4], main_2_step);
  and and_10 (and_13_out[3], main_3_out_4[3], main_2_step);
  and and_11 (and_13_out[2], main_3_out_4[2], main_2_step);
  // memory_small_main main_12: pin names not known; wires that end beside it: main_12_p10[5], rom_1_data[17], main_12_p10[4], rom_1_data[16], main_12_p10[3], rom_1_data[15], main_12_p10[2], main_12_p10[1], rom_1_data[14], main_12_p10[0], rom_1_data[13], rom_1_data[12], main_12_p21[5], rom_1_data[11], main_12_p21[4], rom_1_data[10], main_12_p21[3], main_12_p21[2], rom_1_data[9], main_12_p21[1], main_12_p21[0], button_1_out
  and and_12 (and_13_out[1], main_3_out_4[1], main_2_step);
  and and_13 (and_13_out[0], main_3_out_4[0], main_2_step);
  // memory_small_main main_13: pin names not known; wires that end beside it: main_13_p10[5], rom_1_data[8], main_13_p10[4], rom_1_data[7], main_13_p10[3], rom_1_data[6], main_13_p10[2], main_13_p10[1], rom_1_data[5], main_13_p10[0], rom_1_data[4], rom_1_data[3], main_13_p21[5], rom_1_data[2], main_13_p21[4], rom_1_data[1], main_13_p21[3], main_13_p21[2], rom_1_data[0], main_13_p21[1], main_13_p21[0], button_1_out
  input_selector_main main_14 (
    .in_4(and_1_out), .in_1({6{1'b0}}), .in_2({6{1'b0}}), .in_3({6{1'b0}}), .in_5(main_10_to_a),
    .in_6(main_10_to_b), .in_7(main_10_to_c), .out_8(main_14_out_8), .out_9(main_14_out_9),
    .out_10(main_14_out_10));
  input_selector_main main_15 (
    .in_4(main_2_a_b_3), .in_1(main_14_out_8), .in_2(main_14_out_9), .in_3(main_14_out_10), .in_5({6{1'b0}}),
    .in_6({6{1'b0}}), .in_7({{5{1'b0}}, main_4_equality_check[0]}), .out_8(main_15_out_8),
    .out_9(main_15_out_9), .out_10(main_15_out_10));
  input_selector_main main_16 (
    .in_4(main_2_a_b_2), .in_1(main_15_out_8), .in_2(main_15_out_9), .in_3(main_15_out_10), .in_5({6{1'b0}}),
    .in_6({6{1'b0}}), .in_7({{5{1'b0}}, main_5_out_13[0]}), .out_8(main_16_out_8), .out_9(main_16_out_9),
    .out_10(main_16_out_10));
  input_selector_main main_17 (
    .in_4(main_2_a_b), .in_1(main_16_out_8), .in_2(main_16_out_9), .in_3(main_16_out_10), .in_5({6{1'b0}}),
    .in_6({6{1'b0}}), .in_7({{5{1'b0}}, main_6_out_13[0]}), .out_8(main_17_out_8), .out_9(main_17_out_9),
    .out_10(main_17_out_10));
  input_selector_main main_18 (
    .in_4(main_2_invert), .in_1(main_17_out_8), .in_2(main_17_out_9), .in_3(main_17_out_10),
    .in_5({6{1'b0}}), .in_6({6{1'b0}}), .in_7(main_7_out_12), .out_8(main_18_out_8), .out_9(main_18_out_9),
    .out_10(main_18_out_10));
  input_selector_main main_19 (
    .in_4(main_2_insert), .in_1(main_18_out_8), .in_2(main_18_out_9), .in_3(main_18_out_10), .in_5(in_1),
    .in_6(in_2), .in_7(in_3), .out_8(main_19_out_8), .out_9(main_19_out_9), .out_10(main_19_out_10));
  input_selector_main main_20 (
    .in_4(main_2_add), .in_1(main_19_out_8), .in_2(main_19_out_9), .in_3(main_19_out_10), .in_5({6{1'b0}}),
    .in_6({6{1'b0}}), .in_7(main_9_out_19), .out_8(main_11_p21), .out_9(main_12_p21), .out_10(main_13_p21));

  // Notes on the sheet:
  //   Init2 (Set value to 1 to initialise after init is pressed)
  //   contents of rom_1 (hex, n*v repeats v):
  //   0 511a1 0 52187 0 94a6 0 0 51a87 0 40005 0 32400 10*0 40005 0 51a87 0 32400
endmodule
